// Digital circuit SOAL NO 1 UTS _1.1.dig as structural Verilog
module SOAL_NO_1_UTS__1_1 (
  input  A,
  input  B,
  input  C,
  output Y
);

  wire and_1_out, and_2_out, and_3_out, and_4_out, and_5_out, nor_1_out, or_1_out;

  and and_1 (and_1_out, A, B);
  and and_2 (and_2_out, A, C);
  and and_3 (and_3_out, B, C);
  nor nor_1 (nor_1_out, A, B, C);
  and and_4 (and_4_out, A, B, C);
  or or_1 (or_1_out, and_1_out, and_2_out, and_3_out);
  and and_5 (and_5_out, or_1_out, nor_1_out);
  or or_2 (Y, and_5_out, and_4_out);

  // Notes on the sheet:
  //   RIZKY DWI GUSTIANDI
  //   (AB+AC+BC)'(A+B+C)+ABC
endmodule
