// Digital circuit SOAL NO 5 UTS_1.5.dig as structural Verilog
module SOAL_NO_5_UTS_1_5 (
  input  A,
  input  B,
  input  C,
  input  D,
  output out_5
);

  wire and_1_out, and_2_out, and_3_out, and_4_out, not_1_out, not_2_out, not_3_out, not_4_out;

  not not_1 (not_1_out, A);
  not not_2 (not_2_out, B);
  not not_3 (not_3_out, C);
  not not_4 (not_4_out, D);
  and and_1 (and_1_out, not_1_out, not_2_out, not_4_out);
  and and_2 (and_2_out, B, C, D);
  and and_3 (and_3_out, not_1_out, not_4_out);
  and and_4 (and_4_out, not_2_out, not_3_out, not_4_out);
  or or_1 (out_5, and_1_out, and_4_out, and_2_out, and_3_out);

  // Notes on the sheet:
  //   RIZKY DWI GUSTIANDI
  //   A'B'D'+A'D+BCD+BC'D'
endmodule
